# Fritzing sketch Board Connections (saved by Fritzing 0.9.3b)
circuit board: 8.46667cm x 5.64444cm
breadboards: 2

parts:
  Part1 = Arduino Uno (Rev3)
  RHT1 = Humidity and Temperature Sensor RHT03
  R1 = Resistor [tolerance=±5% resistance=10k package=THT]
  Part2 = Adafruit Thermocouple Amplifier with 1-Wire Breakout Board - MAX31850K [part_number="Adafruit #1727"]
  Part3 = Adafruit Thermocouple Amplifier with 1-Wire Breakout Board - MAX31850K [part_number="Adafruit #1727"]
  Part5 = Adafruit Thermocouple Amplifier with 1-Wire Breakout Board - MAX31850K [part_number="Adafruit #1727"]
  Part4 = Adafruit Thermocouple Amplifier with 1-Wire Breakout Board - MAX31850K [part_number="Adafruit #1727"]
  Part7 = Adafruit Thermocouple Amplifier with 1-Wire Breakout Board - MAX31850K [part_number="Adafruit #1727"]
  Part6 = Adafruit Thermocouple Amplifier with 1-Wire Breakout Board - MAX31850K [part_number="Adafruit #1727"]
  U1 = mystery part, 12 pins [chip_label=TXB0104-Repl]  # not connected
  Part8 = Adafruit Datalogger Shield v1 [part_number="Adafruit #1141"]
  U2 = mystery part, 5 pins [chip_label="Wind Sensor-R"]
  U3 = mystery part, 5 pins [chip_label="Wind Sensor-R"]
  U4 = mystery part, 5 pins [chip_label="Wind Sensor-R"]
  U5 = mystery part, 2 pins [chip_label=CO2]

nets:
  N1: Part1.A0, U2.pin5
  N2: Part1.A1, U3.pin5
  N3: Part1.A2, U4.pin5
  N4: Part1.A3, U5.pin2
  N5: Part1.D10_PWM/SS, Part8.SD_CS
  N6: Part1.D11_PWM/MOSI, Part8.MOSI
  N7: Part1.D12/MISO, Part8.MISO
  N8: Part1.D13/SCK, Part8.SCK
  GND: Part1.GND, RHT1.GND_2, Part2.GND, Part3.GND, Part5.GND, Part4.GND, Part7.GND, Part6.GND, U2.pin1, U3.pin1, U4.pin1, U5.pin1
  N9: Part1.D7, RHT1.Data-signal, R1.Pin_1
  N10: Part1.3V3, U2.pin2, U3.pin2, U4.pin2
  VIN: Part1.5V, RHT1.Vcc, R1.Pin_0, Part2.VIN, Part3.VIN, Part5.VIN, Part7.VIN, Part6.VIN
  N11: Part2.DATA, Part3.DATA, Part5.DATA, Part4.DATA, Part7.DATA, Part6.DATA

notes:
  Based on:
  https://learn.adafruit.com/adafruit-1-wire-thermocouple-amplifier-max31850k/wiring-and-test
  Notes:
  https://learn.adafruit.com/adafruit-data-logger-shield/overview
  Bases on:
  https://howtomechatronics.com/tutorials/arduino/d
  Notes from:
  https://moderndevice.com/product/wind-sensor/
  CO2 Sensor Dummy Replacer
  Guessing that we are reading data throug an analog input, not UART/USB

custom parts:
  Adafruit Thermocouple Amplifier with 1-Wire Breakout Board - MAX31850K: Thermocouples are very sensitive, requiring a good amplifier with a cold-compensation reference. So far we've carried the very nice MAX31855 which is an SPI interface thermocouple amplifier. The '855 is great but if you have a lot of thermocouples to measure it isn't terribly easy to use. That's why we are also carrying the new '850 model from Maxim - it's a "1-Wire" thermocouple amp which can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
  Adafruit Datalogger Shield v1: Here's a handy Arduino shield: we've had a lot of people looking for a dedicated and well-designed data logging shield. We worked hard to engineer an inexpensive but well-rounded design. Not only is it easy to assemble and customize, it also comes with great documentation and libraries. New! we now are carrying an 'assembled' version of this shield, with all the components pre-soldered. NOTE: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
